# Fritzing sketch CurrentConection_wifi-ESP32 (saved by Fritzing 0.9.3b)

parts:
  VCC1 = 4 x AAA Battery Mount
  M1 = RioRand LM2596
  L298N1 = L298N DC motor driver
  L298N2 = L298N DC motor driver
  M2 = DOIT Esp32 DevKit v1 (30 pins long, 11 pins width) [part_number=ESP32S-PIN30]
  HLK-PM1 = HLK-PM12 [part_number=HLK-PM12]
  DC_Mot_Enc1 = DC Motor with two-phase hall-encoder [part_number=VT-E-G25A-06-177E]
  DC_Mot_Enc2 = DC Motor with two-phase hall-encoder [part_number=VT-E-G25A-06-177E]
  DC_Mot_Enc3 = DC Motor with two-phase hall-encoder [part_number=VT-E-G25A-06-177E]

nets:
  GND: VCC1.-, M1.Pin_2, M1.Pin_4, L298N1.GND, L298N2.GND, M2.GND, HLK-PM1.-Vo
  12V: VCC1.+, M1.Pin_1, L298N1.12V, L298N2.12V
  N1: M1.Pin_3, M2.VIN
  N2: L298N1.OUT1, DC_Mot_Enc1.pin2
  N3: L298N1.OUT2, DC_Mot_Enc1.pin1
  N4: L298N1.OUT3, DC_Mot_Enc2.pin2
  N5: L298N1.OUT4, DC_Mot_Enc2.pin1
  N6: L298N1.ENA, M2.D35
  N7: L298N1.ENB, M2.D27
  N8: L298N1.IN1, M2.D32
  N9: L298N1.IN2, M2.D33
  N10: L298N1.IN3, M2.D25
  N11: L298N1.IN4, M2.D26
  N12: L298N2.OUT3, DC_Mot_Enc3.pin2
  N13: L298N2.OUT4, DC_Mot_Enc3.pin1
  N14: L298N2.ENA, M2.D14
  N15: L298N2.IN1, M2.D12
  N16: L298N2.IN2, M2.D13

notes:
  AC/DC power soruce representation
  12V Battery representation
  Regulate to 3.3V

custom parts:
  L298N DC motor driver: 2x DC motor driver with 78M05 positive voltage regulator (7..35 V) L298N: max 46 V, 2 A Set 5 V Enable jumper to enable 5 V regultor (needed for the L298N) and +5 V output at screw terminal or supply external +5 V at screw terminal Set ENA and/or ENB to +5 V to enable motor permanently or supply ENA and/or ENB with PWM signal IN1 and IN2 set rotation directory for motor A (OUT1/OUT2) IN2 and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
  DOIT Esp32 DevKit v1 (30 pins long, 11 pins width): The DOIT Esp32 DevKit v1 is one of the development board created by DOIT to evaluate the ESP-WROOM-32 module. It is based on the ESP32 microcontroller that boasts Wifi, Bluetooth, Ethernet and Low Power support all in a single chip. (vanepp) made breadboard work, adjusted pin numbering and labels and reduced size of schematic and cleaned up pcb. This chip is 30pins long (2 x15) and 11 pins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
