# Fritzing sketch FritzingSketch (saved by Fritzing 0.9.3b)

parts:
  Part1 = Adafruit HUZZAH32 ESP32 Feather [part_number="Adafruit #3405"]
  L298N1 = L298N DC motor driver
  HLK-PM1 = HLK-PM01
  BAT1 = BC9VPC [package=bc9vpc]
  DC_Mot_Enc1 = DC Motor with two-phase hall-encoder [part_number=VT-E-G25A-06-177E]
  U1 = LM2596 step down module
  DC_Mot_Enc2 = DC Motor with two-phase hall-encoder [part_number=VT-E-G25A-06-177E]
  DC_Mot_Enc3 = DC Motor with two-phase hall-encoder [part_number=VT-E-G25A-06-177E]
  L298N2 = L298N DC motor driver

nets:
  N1: Part1.IO21, L298N1.ENA
  GND: Part1.GND, L298N1.GND, HLK-PM1.-Vo, BAT1.V-, U1.IN-, U1.OUT-, L298N2.GND
  N2: Part1.VBAT, U1.OUT+
  N3: Part1.IO12_A11, L298N1.IN1
  N4: Part1.IO27_A10, L298N1.IN2
  N5: Part1.IO33_A9, L298N1.IN3
  N6: Part1.IO15_A8, L298N1.IN4
  N7: Part1.IO32_A7, L298N1.ENB
  N8: Part1.IO14_A6, L298N2.ENA
  N9: Part1.SCL, L298N2.IN1
  N10: Part1.SDA, L298N2.IN2
  N11: L298N1.OUT1, DC_Mot_Enc1.pin2
  N12: L298N1.OUT2, DC_Mot_Enc1.pin1
  N13: L298N1.OUT3, DC_Mot_Enc3.pin2
  N14: L298N1.OUT4, DC_Mot_Enc3.pin1
  12V: L298N1.12V, HLK-PM1.+Vo, BAT1.V+, U1.IN+, L298N2.12V
  N15: DC_Mot_Enc2.pin2, L298N2.OUT1

notes:
  V_out: 4.2V

custom parts:
  L298N DC motor driver: 2x DC motor driver with 78M05 positive voltage regulator (7..35 V) L298N: max 46 V, 2 A Set 5 V Enable jumper to enable 5 V regultor (needed for the L298N) and +5 V output at screw terminal or supply external +5 V at screw terminal Set ENA and/or ENB to +5 V to enable motor permanently or supply ENA and/or ENB with PWM signal IN1 and IN2 set rotation directory for motor A (OUT1/OUT2) IN2 and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
  LM2596 step down module: LM2596 DC-DC step down power supply module 3 A.
